# Fritzing sketch Bicyduino fritzing (saved by Fritzing 0.9.2b)
breadboards: 1

parts:
  Pro_Micro1 = Pro Micro
  S1 = Reed switch [package=THT]  # not connected
  S2 = Reed switch [package=THT]
  Composant1 = Triple Axis Accelerometer Breakout - ADXL335  # not connected

nets:
  N1: Pro_Micro1.D2, S2.pin_2

custom parts:
  Pro Micro: The SparkFun Pro Micro is a complete USB-based microcontoller development system, in a very small footprint, capable of implementing many types of projects. All programming can be done via the USB port.
